# Fritzing sketch weatherStation (saved by Fritzing 1.0.4)
breadboards: 1

parts:
  5461AS = HS420561K [part_number=HS420561K package="DIP (Dual Inline) [THT]"]
  DHT11 = DHT11 Humitidy and Temperature Sensor (3 pins)
  Push_Button = Momentary Switch [package=ksa_sealed_tac_switch]
  part = Resistor [tolerance=±5% resistance=220 package="0805 [SMD]"]
  part_2 = Resistor [tolerance=±5% resistance=220 package="0805 [SMD]"]
  part_3 = Resistor [tolerance=±5% resistance=220 package="0805 [SMD]"]
  part_4 = Resistor [tolerance=±5% resistance=220 package="0805 [SMD]"]
  10kΩ = Resistor [tolerance=±5% resistance=220 package="0805 [SMD]"]
  Part1 = Arduino Uno (Rev3)

nets:
  N1: 5461AS.pin1, Part1.D8
  N2: 5461AS.pin2, Part1.D7
  N3: 5461AS.pin3, Part1.D11_PWM/MOSI
  N4: 5461AS.pin4, Part1.D6_PWM
  N5: 5461AS.pin5, Part1.D10_PWM/SS
  N6: 5461AS.pin6, part_4.Pin_1
  N7: 5461AS.pin7, Part1.D5_PWM
  N8: 5461AS.pin8, part_3.Pin_1
  N9: 5461AS.pin_9, part_2.Pin_1
  N10: 5461AS.pin_10, Part1.D9_PWM
  N11: 5461AS.pin_11, Part1.D4
  N12: 5461AS.pin_12, part.Pin_1
  N13: DHT11.Plus, Part1.A0
  N14: DHT11.Signal, Push_Button.1, Part1.5V
  GND: DHT11.Gnd, 10kΩ.Pin_0, Part1.GND
  N15: Push_Button.3, 10kΩ.Pin_1
  N16: Push_Button.4, Part1.D3_PWM
  N17: part.Pin_0, Part1.A5/SCL
  N18: part_2.Pin_0, Part1.A4/SDA
  N19: part_3.Pin_0, Part1.A3
  N20: part_4.Pin_0, Part1.A2

custom parts:
  DHT11 Humitidy and Temperature Sensor (3 pins): DHT11 Humidity and Temperature Sensor (3 pins).
